// Logisim project Classlib.circ as structural Verilog: 12 circuits, main circuit HA_1
module HA_1 (
  input  A,
  input  B,
  output COUT__AB,
  output SUM__AB_prime__A_prime_B
);

  wire A_prime_B_out, AB_prime_out, not_1_out, not_2_out;

  not not_1 (not_1_out, B);
  not not_2 (not_2_out, A);
  and AB_prime (AB_prime_out, A, not_1_out);
  and A_prime_B (A_prime_B_out, not_2_out, B);
  and AB (COUT__AB, B, A);
  or or_1 (SUM__AB_prime__A_prime_B, AB_prime_out, A_prime_B_out);
endmodule

module FA_1 (
  input  A,
  input  Cin,
  input  B,
  output SUM,
  output Cout
);

  wire AB_out, XAB_out, XABC_out;

  and AB (AB_out, B, A);
  xor XAB (XAB_out, A, B);
  xor XABXC (SUM, Cin, XAB_out);
  and XABC (XABC_out, Cin, XAB_out);
  or or_1 (Cout, XABC_out, AB_out);
endmodule

module FA_4 (
  input  A0,
  input  A1,
  input  A2,
  input  A3,
  input  B0,
  input  B1,
  input  B2,
  input  B3,
  input  CIN,
  output S0,
  output S1,
  output S2,
  output S3,
  output COUT
);

  wire fa_1_1_cout, fa_1_2_cout, fa_1_3_cout;

  FA_1 fa_1_1 (.A(A0), .Cin(CIN), .B(B0), .SUM(S0), .Cout(fa_1_1_cout));
  FA_1 fa_1_2 (.A(A1), .Cin(fa_1_1_cout), .B(B1), .SUM(S1), .Cout(fa_1_2_cout));
  FA_1 fa_1_3 (.A(A2), .Cin(fa_1_2_cout), .B(B2), .SUM(S2), .Cout(fa_1_3_cout));
  FA_1 fa_1_4 (.A(A3), .Cin(fa_1_3_cout), .B(B3), .SUM(S3), .Cout(COUT));

  // Notes on the sheet:
  //   Full Adder
endmodule

// B
module INC_4 (
  input  CIN,
  input  A0,
  input  A1,
  input  A2,
  input  A3,
  output COUT,
  output S0,
  output S1,
  output S2,
  output S3
);

  wire ha_1_1_cout__ab, ha_1_2_cout__ab, ha_1_3_cout__ab;

  HA_1 ha_1_1 (.A(CIN), .B(A0), .COUT__AB(ha_1_1_cout__ab), .SUM__AB_prime__A_prime_B(S0));
  HA_1 ha_1_2 (.A(ha_1_1_cout__ab), .B(A1), .COUT__AB(ha_1_2_cout__ab), .SUM__AB_prime__A_prime_B(S1));
  HA_1 ha_1_3 (.A(ha_1_2_cout__ab), .B(A2), .COUT__AB(ha_1_3_cout__ab), .SUM__AB_prime__A_prime_B(S2));
  HA_1 ha_1_4 (.A(ha_1_3_cout__ab), .B(A3), .COUT__AB(COUT), .SUM__AB_prime__A_prime_B(S3));

  // Notes on the sheet:
  //   4-Bit Increment Schematic
endmodule

module Negate (
  input  PASS_prime_2_sCOMP,
  input  in_2,
  input  in_3,
  input  in_4,
  input  in_5,
  output out_6,
  output out_7,
  output out_8,
  output out_9,
  output out_10
);

  wire xor_1_out, xor_2_out, xor_3_out, xor_4_out;

  xor xor_1 (xor_1_out, PASS_prime_2_sCOMP, in_2);
  xor xor_2 (xor_2_out, PASS_prime_2_sCOMP, in_3);
  xor xor_3 (xor_3_out, PASS_prime_2_sCOMP, in_4);
  xor xor_4 (xor_4_out, PASS_prime_2_sCOMP, in_5);
  INC_4 inc_4_1 (
    .CIN(PASS_prime_2_sCOMP), .A0(xor_4_out), .A1(xor_3_out), .A2(xor_2_out), .A3(xor_1_out), .COUT(out_6),
    .S0(out_7), .S1(out_8), .S2(out_9), .S3(out_10));
endmodule

module MUX_1 (
  input  A,
  input  A_B_prime,
  input  B,
  output Y
);

  wire and_1_out, and_2_out, not_1_out;

  and and_1 (and_1_out, A, A_B_prime);
  not not_1 (not_1_out, A_B_prime);
  and and_2 (and_2_out, not_1_out, B);
  or or_1 (Y, and_1_out, and_2_out);
endmodule

module MUX_4 (
  input  S,
  input  A3,
  input  B3,
  input  A2,
  input  B2,
  input  A1,
  input  B1,
  input  A0,
  input  B0,
  output Y3,
  output Y2,
  output Y1,
  output Y0
);

  MUX_1 mux_1_1 (.A(A3), .A_B_prime(S), .B(B3), .Y(Y3));
  MUX_1 mux_1_2 (.A(A2), .A_B_prime(S), .B(B2), .Y(Y2));
  MUX_1 mux_1_3 (.A(A1), .A_B_prime(S), .B(B1), .Y(Y1));
  MUX_1 mux_1_4 (.A(A0), .A_B_prime(S), .B(B0), .Y(Y0));

  // Notes on the sheet:
  //   MUX_4 A/B' = 0, A = 12, B = 7
endmodule

module DEMUX_1 (
  input  I,
  input  S,
  output A,
  output B
);

  and and_1 (A, I, S);
  and and_2 (B, I, ~S);  // AND_Gate

  // Notes on the sheet:
  //   1-Bit Demultiplexer SOP Form
  //   I = IN
  //   S = Switch (A/B')
endmodule

module DEMUX_4 (
  input  D3,
  input  D2,
  input  D1,
  input  D0,
  input  A_B,
  output A3,
  output B3,
  output A2,
  output B2,
  output A1,
  output B1,
  output A0,
  output B0
);

  DEMUX_1 demux_1_1 (.S(A_B), .B(B3), .I(D3), .A(A3));
  DEMUX_1 demux_1_2 (.S(A_B), .B(B2), .I(D2), .A(A2));
  DEMUX_1 demux_1_3 (.S(A_B), .B(B1), .I(D1), .A(A1));
  DEMUX_1 demux_1_4 (.S(A_B), .B(B0), .I(D0), .A(A0));
endmodule

// ADD_SUB
module ADD_SUBT (
  input  Switch,
  input  B3,
  input  B2,
  input  B1,
  input  B0,
  input  A3,
  input  A2,
  input  A1,
  input  A0,
  output S3,
  output S2,
  output S1,
  output S0,
  output out_14
);

  wire inc_4_1_s0, inc_4_1_s1, inc_4_1_s2, inc_4_1_s3, xor_1_out, xor_2_out, xor_3_out, xor_4_out;

  xor xor_1 (xor_1_out, Switch, B3);
  xor xor_2 (xor_2_out, Switch, B2);
  xor xor_3 (xor_3_out, Switch, B1);
  xor xor_4 (xor_4_out, Switch, B0);
  INC_4 inc_4_1 (
    .CIN(Switch), .A0(xor_4_out), .A1(xor_3_out), .A2(xor_2_out), .A3(xor_1_out), .S0(inc_4_1_s0),
    .S1(inc_4_1_s1), .S2(inc_4_1_s2), .S3(inc_4_1_s3));  // open: COUT
  FA_4 fa_4_1 (
    .CIN(1'b0), .A0(inc_4_1_s0), .A1(inc_4_1_s1), .B0(A0), .B1(A1), .A2(inc_4_1_s2), .B2(A2),
    .A3(inc_4_1_s3), .B3(A3), .S0(S0), .S1(S1), .S2(S2), .S3(S3), .COUT(out_14));
  Hex_Digit_Display hex_digit_display_1 (.value({S3, S2, S1, S0}));  // open: dp

  // Notes on the sheet:
  //   Format goes X = A + B or A - B, order matters!
  //   If 1 = 0001, Bits go A3;A2:A1:A0
endmodule

module SHIFT (
  input  SHAMT1,
  input  SHAMT0,
  input  L_R_prime,
  input  SHNUM3,
  input  SHNUM2,
  input  SHNUM1,
  input  SHNUM0,
  output SHOUT3,
  output SHOUT2,
  output SHOUT1,
  output SHOUT0
);

  wire and_1_out, and_2_out, and_3_out, mux_4_1_y0, mux_4_1_y1, mux_4_1_y2, mux_4_1_y3, mux_4_2_y0,
       mux_4_2_y1, mux_4_2_y2, mux_4_2_y3, mux_4_3_y0, mux_4_3_y1, mux_4_3_y2, mux_4_3_y3, mux_4_4_y0,
       mux_4_4_y1, mux_4_4_y2, mux_4_4_y3, mux_4_5_y0, mux_4_5_y1, mux_4_5_y2, mux_4_5_y3, mux_4_6_y0,
       mux_4_6_y1, mux_4_6_y2, mux_4_6_y3, not_1_out, not_2_out, or_1_out, or_2_out;

  and and_1 (and_1_out, SHAMT0, not_1_out);
  not not_1 (not_1_out, SHAMT1);
  not not_2 (not_2_out, SHAMT0);
  and and_2 (and_2_out, not_2_out, SHAMT1);
  and and_3 (and_3_out, SHAMT1, SHAMT0);
  MUX_4 mux_4_1 (
    .A3(SHNUM2), .B3(SHNUM3), .A2(SHNUM1), .B2(SHNUM2), .A1(SHNUM0), .B1(SHNUM1), .A0(1'b0), .B0(SHNUM0),
    .Y3(mux_4_1_y3), .Y2(mux_4_1_y2), .Y1(mux_4_1_y1), .Y0(mux_4_1_y0), .S(or_2_out));
  MUX_4 mux_4_2 (
    .A3(1'b0), .B3(SHNUM3), .A2(SHNUM3), .B2(SHNUM2), .A1(SHNUM2), .B1(SHNUM1), .A0(SHNUM1), .B0(SHNUM0),
    .Y3(mux_4_2_y3), .Y2(mux_4_2_y2), .Y1(mux_4_2_y1), .Y0(mux_4_2_y0), .S(or_2_out));
  LED led_1 (.in(and_3_out));
  LED led_2 (.in(and_1_out));
  LED led_3 (.in(and_2_out));
  or or_1 (or_1_out, and_3_out, and_2_out);
  or or_2 (or_2_out, and_2_out, and_1_out, and_3_out);
  MUX_4 mux_4_3 (
    .A3(mux_4_1_y2), .B3(mux_4_1_y3), .A2(mux_4_1_y1), .B2(mux_4_1_y2), .A1(mux_4_1_y0), .B1(mux_4_1_y1),
    .A0(1'b0), .B0(mux_4_1_y0), .Y3(mux_4_3_y3), .Y2(mux_4_3_y2), .Y1(mux_4_3_y1), .Y0(mux_4_3_y0),
    .S(or_1_out));
  MUX_4 mux_4_4 (
    .A3(1'b0), .B3(mux_4_2_y3), .A2(mux_4_2_y3), .B2(mux_4_2_y2), .A1(mux_4_2_y2), .B1(mux_4_2_y1),
    .A0(mux_4_2_y1), .B0(mux_4_2_y0), .Y3(mux_4_4_y3), .Y2(mux_4_4_y2), .Y1(mux_4_4_y1), .Y0(mux_4_4_y0),
    .S(or_1_out));
  LED led_4 (.in(and_3_out));
  LED led_5 (.in(or_1_out));
  LED led_6 (.in(or_2_out));
  MUX_4 mux_4_5 (
    .A3(mux_4_3_y2), .B3(mux_4_3_y3), .A2(mux_4_3_y1), .B2(mux_4_3_y2), .A1(mux_4_3_y0), .B1(mux_4_3_y1),
    .A0(1'b0), .B0(mux_4_3_y0), .Y3(mux_4_5_y3), .Y2(mux_4_5_y2), .Y1(mux_4_5_y1), .Y0(mux_4_5_y0),
    .S(and_3_out));
  MUX_4 mux_4_6 (
    .A3(1'b0), .B3(mux_4_4_y3), .A2(mux_4_4_y3), .B2(mux_4_4_y2), .A1(mux_4_4_y2), .B1(mux_4_4_y1),
    .A0(mux_4_4_y1), .B0(mux_4_4_y0), .Y3(mux_4_6_y3), .Y2(mux_4_6_y2), .Y1(mux_4_6_y1), .Y0(mux_4_6_y0),
    .S(and_3_out));
  MUX_4 mux_4_7 (
    .A3(mux_4_5_y3), .B3(mux_4_6_y3), .A2(mux_4_5_y2), .B2(mux_4_6_y2), .A1(mux_4_5_y1), .B1(mux_4_6_y1),
    .A0(mux_4_5_y0), .B0(mux_4_6_y0), .Y3(SHOUT3), .Y2(SHOUT2), .Y1(SHOUT1), .Y0(SHOUT0), .S(L_R_prime));
endmodule

module Multiply_1 (
  input  in_1,
  input  in_2,
  input  in_3,
  input  in_4,
  input  in_5,
  input  in_6,
  input  in_7,
  input  in_8,
  output out_9,
  output out_10,
  output out_11,
  output out_12,
  output out_13,
  output out_14,
  output out_15,
  output out_16
);

  wire fa_4_1_s0, fa_4_1_s1, fa_4_1_s2, fa_4_1_s3, fa_4_2_s0, fa_4_2_s1, fa_4_2_s2, fa_4_2_s3, fa_4_3_cout,
       fa_4_3_s0, fa_4_3_s1, fa_4_3_s2, fa_4_3_s3, fa_4_4_s0, fa_4_4_s1, fa_4_4_s2, fa_4_4_s3, fa_4_5_cout,
       fa_4_5_s0, fa_4_5_s1, fa_4_5_s2, fa_4_5_s3, fa_4_6_s0, fa_4_6_s1, fa_4_6_s2, fa_4_6_s3, fa_4_7_cout,
       fa_4_7_s0, fa_4_7_s1, fa_4_7_s2, fa_4_7_s3, fa_4_9_cout, mux_4_6_y0, mux_4_6_y1, mux_4_6_y2,
       mux_4_6_y3, mux_4_7_y0, mux_4_7_y1, mux_4_7_y2, mux_4_7_y3, xor_1_out, xor_2_out, xor_3_out,
       xor_4_out, xor_5_out, xor_6_out, xor_7_out, xor_8_out, xor_9_out;
  wire [3:0] add_subt_1_s0, add_subt_2_s0, mux_4_1_y0, mux_4_2_y0, mux_4_3_y0, mux_4_4_y0, mux_4_5_y0;

  Hex_Digit_Display hex_digit_display_1 (.value({in_1, in_2, in_3, in_4}));  // open: dp
  Hex_Digit_Display hex_digit_display_2 (.value({in_5, in_6, in_7, in_8}));  // open: dp
  ADD_SUBT add_subt_1 (
    .Switch(in_1), .B3(in_1), .B2(in_2), .B1(in_3), .B0(in_4), .A3(1'b0), .A2(1'b0), .A1(1'b0), .A0(1'b0),
    .S3(add_subt_1_s0[3]), .S2(add_subt_1_s0[2]), .S1(add_subt_1_s0[1]), .S0(add_subt_1_s0[0]));  // open: out_14
  ADD_SUBT add_subt_2 (
    .Switch(in_5), .B3(in_5), .B2(in_6), .B1(in_7), .B0(in_8), .A3(1'b0), .A2(1'b0), .A1(1'b0), .A0(1'b0),
    .S3(add_subt_2_s0[3]), .S2(add_subt_2_s0[2]), .S1(add_subt_2_s0[1]), .S0(add_subt_2_s0[0]));  // open: out_14
  Hex_Digit_Display hex_digit_display_3 (.value(add_subt_1_s0));  // open: dp
  Hex_Digit_Display hex_digit_display_4 (.value(add_subt_2_s0));  // open: dp
  FA_4 fa_4_1 (
    .CIN(1'b0), .A0(1'b0), .A1(1'b0), .B0(add_subt_1_s0[0]), .B1(add_subt_1_s0[1]), .A2(1'b0),
    .B2(add_subt_1_s0[2]), .A3(1'b0), .B3(add_subt_1_s0[3]), .S0(fa_4_1_s0), .S1(fa_4_1_s1), .S2(fa_4_1_s2),
    .S3(fa_4_1_s3));  // open: COUT
  LED led_1 (.in(add_subt_2_s0[0]));
  MUX_4 mux_4_1 (
    .A3(fa_4_1_s3), .B3(1'b0), .A2(fa_4_1_s2), .B2(1'b0), .A1(fa_4_1_s1), .B1(1'b0), .A0(fa_4_1_s0),
    .B0(1'b0), .Y3(mux_4_1_y0[3]), .Y2(mux_4_1_y0[2]), .Y1(mux_4_1_y0[1]), .Y0(mux_4_1_y0[0]),
    .S(add_subt_2_s0[0]));
  FA_4 fa_4_2 (
    .CIN(fa_4_3_cout), .A0(1'b0), .A1(1'b0), .B0(add_subt_1_s0[3]), .B1(1'b0), .A2(1'b0), .B2(1'b0),
    .A3(1'b0), .B3(1'b0), .S0(fa_4_2_s0), .S1(fa_4_2_s1), .S2(fa_4_2_s2), .S3(fa_4_2_s3));  // open: COUT
  FA_4 fa_4_3 (
    .CIN(1'b0), .A0(mux_4_1_y0[0]), .A1(mux_4_1_y0[1]), .B0(1'b0), .B1(add_subt_1_s0[0]), .A2(mux_4_1_y0[2]),
    .B2(add_subt_1_s0[1]), .A3(mux_4_1_y0[3]), .B3(add_subt_1_s0[2]), .S0(fa_4_3_s0), .S1(fa_4_3_s1),
    .S2(fa_4_3_s2), .S3(fa_4_3_s3), .COUT(fa_4_3_cout));
  LED led_2 (.in(add_subt_2_s0[1]));
  MUX_4 mux_4_2 (
    .A3(fa_4_2_s3), .B3(1'b0), .A2(fa_4_2_s2), .B2(1'b0), .A1(fa_4_2_s1), .B1(1'b0), .A0(fa_4_2_s0),
    .B0(1'b0), .Y3(mux_4_2_y0[3]), .Y2(mux_4_2_y0[2]), .Y1(mux_4_2_y0[1]), .Y0(mux_4_2_y0[0]),
    .S(add_subt_2_s0[1]));
  MUX_4 mux_4_3 (
    .A3(fa_4_3_s3), .B3(mux_4_1_y0[3]), .A2(fa_4_3_s2), .B2(mux_4_1_y0[2]), .A1(fa_4_3_s1),
    .B1(mux_4_1_y0[1]), .A0(fa_4_3_s0), .B0(mux_4_1_y0[0]), .Y3(mux_4_3_y0[3]), .Y2(mux_4_3_y0[2]),
    .Y1(mux_4_3_y0[1]), .Y0(mux_4_3_y0[0]), .S(add_subt_2_s0[1]));
  Hex_Digit_Display hex_digit_display_5 (.value(mux_4_1_y0));  // open: dp
  FA_4 fa_4_4 (
    .CIN(fa_4_5_cout), .A0(mux_4_2_y0[0]), .A1(mux_4_2_y0[1]), .B0(add_subt_1_s0[2]), .B1(add_subt_1_s0[3]),
    .A2(mux_4_2_y0[2]), .B2(1'b0), .A3(mux_4_2_y0[3]), .B3(1'b0), .S0(fa_4_4_s0), .S1(fa_4_4_s1),
    .S2(fa_4_4_s2), .S3(fa_4_4_s3));  // open: COUT
  FA_4 fa_4_5 (
    .CIN(1'b0), .A0(mux_4_3_y0[0]), .A1(mux_4_3_y0[1]), .B0(1'b0), .B1(1'b0), .A2(mux_4_3_y0[2]),
    .B2(add_subt_1_s0[0]), .A3(mux_4_3_y0[3]), .B3(add_subt_1_s0[1]), .S0(fa_4_5_s0), .S1(fa_4_5_s1),
    .S2(fa_4_5_s2), .S3(fa_4_5_s3), .COUT(fa_4_5_cout));
  Hex_Digit_Display hex_digit_display_6 (.value(mux_4_2_y0));  // open: dp
  Hex_Digit_Display hex_digit_display_7 (.value(mux_4_3_y0));  // open: dp
  MUX_4 mux_4_4 (
    .A3(fa_4_4_s3), .B3(mux_4_2_y0[3]), .A2(fa_4_4_s2), .B2(mux_4_2_y0[2]), .A1(fa_4_4_s1),
    .B1(mux_4_2_y0[1]), .A0(fa_4_4_s0), .B0(mux_4_2_y0[0]), .Y3(mux_4_4_y0[3]), .Y2(mux_4_4_y0[2]),
    .Y1(mux_4_4_y0[1]), .Y0(mux_4_4_y0[0]), .S(add_subt_2_s0[2]));
  MUX_4 mux_4_5 (
    .A3(fa_4_5_s3), .B3(mux_4_3_y0[3]), .A2(fa_4_5_s2), .B2(mux_4_3_y0[2]), .A1(fa_4_5_s1),
    .B1(mux_4_3_y0[1]), .A0(fa_4_5_s0), .B0(mux_4_3_y0[0]), .Y3(mux_4_5_y0[3]), .Y2(mux_4_5_y0[2]),
    .Y1(mux_4_5_y0[1]), .Y0(mux_4_5_y0[0]), .S(add_subt_2_s0[2]));
  LED led_3 (.in(add_subt_2_s0[2]));
  FA_4 fa_4_6 (
    .CIN(fa_4_7_cout), .A0(mux_4_4_y0[0]), .A1(mux_4_4_y0[1]), .B0(add_subt_1_s0[1]), .B1(add_subt_1_s0[2]),
    .A2(mux_4_4_y0[2]), .B2(add_subt_1_s0[3]), .A3(mux_4_4_y0[3]), .B3(1'b0), .S0(fa_4_6_s0), .S1(fa_4_6_s1),
    .S2(fa_4_6_s2), .S3(fa_4_6_s3));  // open: COUT
  FA_4 fa_4_7 (
    .CIN(1'b0), .A0(mux_4_5_y0[0]), .A1(mux_4_5_y0[1]), .B0(1'b0), .B1(1'b0), .A2(mux_4_5_y0[2]), .B2(1'b0),
    .A3(mux_4_5_y0[3]), .B3(add_subt_1_s0[0]), .S0(fa_4_7_s0), .S1(fa_4_7_s1), .S2(fa_4_7_s2),
    .S3(fa_4_7_s3), .COUT(fa_4_7_cout));
  Hex_Digit_Display hex_digit_display_8 (.value(mux_4_4_y0));  // open: dp
  xor xor_1 (xor_1_out, in_1, in_5);
  MUX_4 mux_4_6 (
    .A3(fa_4_7_s3), .B3(mux_4_5_y0[3]), .A2(fa_4_7_s2), .B2(mux_4_5_y0[2]), .A1(fa_4_7_s1),
    .B1(mux_4_5_y0[1]), .A0(fa_4_7_s0), .B0(mux_4_5_y0[0]), .Y3(mux_4_6_y3), .Y2(mux_4_6_y2),
    .Y1(mux_4_6_y1), .Y0(mux_4_6_y0), .S(add_subt_2_s0[3]));
  Hex_Digit_Display hex_digit_display_9 (.value(mux_4_5_y0));  // open: dp
  MUX_4 mux_4_7 (
    .A3(fa_4_6_s3), .B3(mux_4_4_y0[3]), .A2(fa_4_6_s2), .B2(mux_4_4_y0[2]), .A1(fa_4_6_s1),
    .B1(mux_4_4_y0[1]), .A0(fa_4_6_s0), .B0(mux_4_4_y0[0]), .Y3(mux_4_7_y3), .Y2(mux_4_7_y2),
    .Y1(mux_4_7_y1), .Y0(mux_4_7_y0), .S(add_subt_2_s0[3]));
  LED led_4 (.in(add_subt_2_s0[3]));
  xor xor_2 (xor_2_out, xor_1_out, mux_4_7_y3);
  xor xor_3 (xor_3_out, xor_1_out, mux_4_7_y2);
  xor xor_4 (xor_4_out, xor_1_out, mux_4_7_y1);
  xor xor_5 (xor_5_out, xor_1_out, mux_4_7_y0);
  xor xor_6 (xor_6_out, xor_1_out, mux_4_6_y3);
  xor xor_7 (xor_7_out, xor_1_out, mux_4_6_y2);
  xor xor_8 (xor_8_out, xor_1_out, mux_4_6_y1);
  xor xor_9 (xor_9_out, xor_1_out, mux_4_6_y0);
  FA_4 fa_4_8 (
    .CIN(fa_4_9_cout), .A0(1'b0), .A1(1'b0), .B0(xor_5_out), .B1(xor_4_out), .A2(1'b0), .B2(xor_3_out),
    .A3(1'b0), .B3(xor_2_out), .S0(out_12), .S1(out_11), .S2(out_10), .S3(out_9));  // open: COUT
  FA_4 fa_4_9 (
    .CIN(xor_1_out), .A0(1'b0), .A1(1'b0), .B0(xor_9_out), .B1(xor_8_out), .A2(1'b0), .B2(xor_7_out),
    .A3(1'b0), .B3(xor_6_out), .S0(out_16), .S1(out_15), .S2(out_14), .S3(out_13), .COUT(fa_4_9_cout));
  Hex_Digit_Display hex_digit_display_10 (.value({out_9, out_10, out_11, out_12}));  // open: dp
  Hex_Digit_Display hex_digit_display_11 (.value({out_13, out_14, out_15, out_16}));  // open: dp
endmodule
